# Fritzing sketch PBL_Example_Circuit_Diagram (saved by Fritzing 0.9.3b)
breadboards: 1

parts:
  Part1 = Arduino Uno (Rev3) - ICSP
  J1 = Piezo Speaker
  S1 = Pushbutton [package="[THT]"]
  LED1 = LED - 3mm [color="Red (633nm)" package="3 mm [THT]"]
  R1 = Resistor [tolerance=±5% resistance=330 package=THT]
  hc-sr1 = hc-sr04

nets:
  N1: Part1.D10_PWM/SS, hc-sr1.Echo
  N2: Part1.D11_PWM/MOSI, hc-sr1.Trig
  GND: Part1.D4, Part1.GND, J1.pin1, S1.Pin_1, S1.Pin_2, S1.Pin_3, S1.Pin_4, R1.Pin_0, hc-sr1.GND
  N3: Part1.D5_PWM, J1.pin2
  N4: Part1.D6_PWM, LED1.anode
  5V: Part1.5V, hc-sr1.VCC
  N5: LED1.cathode, R1.Pin_1

notes:
  U1
  D1
  BZ1
  S1
